// Logisim project 8bit_adder_with_save.circ as structural Verilog: 1 circuit, main circuit main
module main (
  input  [7:0] VALUE_A,
  input  [7:0] VALUE_B,
  input  SAVE_RESULT,
  input  SELECT_SAVE,
  output [7:0] out_5
);

  wire adder_1_cout;
  wire [7:0] Latch_q, n_1_out_4;

  LED led_1 (.in(adder_1_cout));
  n n_1 (.INPUT_A(Latch_q), .INPUT_B(VALUE_B), .A_B(SELECT_SAVE), .out_4(n_1_out_4));
  Adder adder_1 (.a(n_1_out_4), .b(VALUE_A), .out(out_5), .cin(1'b0), .cout(adder_1_cout));
  Register Latch (.D(out_5), .Q(Latch_q), .clk(SAVE_RESULT), .clr(1'b0));  // open: en

  // Notes on the sheet:
  //   Overflow
  //   A-B Switch
endmodule
