// Logisim project 8bit_adder_with_sub.circ as structural Verilog: 1 circuit, main circuit main
module main (
  input  [7:0] INPUT_A,
  input  [7:0] INPUT_B,
  input  SUB,
  output [7:0] RESULT
);

  wire adder_1_cout, xor_1_out;
  wire [7:0] xor_9_out;

  LED OVERFLOW (.in(xor_1_out));
  xor xor_1 (xor_1_out, SUB, adder_1_cout);
  Adder adder_1 (.a(xor_9_out), .b(INPUT_A), .out(RESULT), .cin(SUB), .cout(adder_1_cout));
  xor xor_2 (xor_9_out[7], SUB, INPUT_B[7]);
  xor xor_3 (xor_9_out[6], SUB, INPUT_B[6]);
  xor xor_4 (xor_9_out[4], SUB, INPUT_B[4]);
  xor xor_5 (xor_9_out[5], SUB, INPUT_B[5]);
  xor xor_6 (xor_9_out[3], SUB, INPUT_B[3]);
  xor xor_7 (xor_9_out[2], SUB, INPUT_B[2]);
  xor xor_8 (xor_9_out[1], SUB, INPUT_B[1]);
  xor xor_9 (xor_9_out[0], SUB, INPUT_B[0]);
endmodule
