// Logisim project 4bit_subtractor.circ as structural Verilog: 1 circuit, main circuit main
module main (
  input  A0,
  input  B0,
  input  A1,
  input  B1,
  input  A2,
  input  B2,
  input  A3,
  input  B3,
  output Sum,
  output Sum_2,
  output Sum_3,
  output Sum_4,
  output Cout
);

  wire and_1_out, and_2_out, and_3_out, and_4_out, and_5_out, and_6_out, and_7_out, and_8_out, not_1_out,
       not_2_out, not_3_out, not_4_out, not_5_out, not_6_out, not_7_out, not_8_out, or_1_out, or_2_out,
       or_3_out, xor_1_out, xor_2_out, xor_3_out, xor_4_out;

  not not_1 (not_1_out, A0);
  and and_1 (and_1_out, not_1_out, B0);
  not not_2 (not_2_out, A1);
  not not_3 (not_3_out, A2);
  not not_4 (not_4_out, A3);
  xor xor_1 (xor_1_out, A0, B0);
  not not_5 (not_5_out, xor_1_out);
  xor xor_2 (xor_2_out, A1, B1);
  and and_2 (and_2_out, not_2_out, B1);
  xor xor_3 (xor_3_out, A2, B2);
  and and_3 (and_3_out, not_3_out, B2);
  xor xor_4 (xor_4_out, A3, B3);
  and and_4 (and_4_out, not_4_out, B3);
  and and_5 (and_5_out, not_5_out, 1'b0);
  not not_6 (not_6_out, xor_2_out);
  not not_7 (not_7_out, xor_3_out);
  not not_8 (not_8_out, xor_4_out);
  xor xor_5 (Sum, xor_1_out, 1'b0);
  or or_1 (or_1_out, and_5_out, and_1_out);
  and and_6 (and_6_out, not_6_out, or_1_out);
  and and_7 (and_7_out, not_7_out, or_2_out);
  and and_8 (and_8_out, not_8_out, or_3_out);
  xor xor_6 (Sum_2, xor_2_out, or_1_out);
  or or_2 (or_2_out, and_6_out, and_2_out);
  xor xor_7 (Sum_3, xor_3_out, or_2_out);
  or or_3 (or_3_out, and_7_out, and_3_out);
  xor xor_8 (Sum_4, xor_4_out, or_3_out);
  or or_4 (Cout, and_8_out, and_4_out);
endmodule
