// Logisim project flip_flop.circ as structural Verilog: 1 circuit, main circuit main
module main (
  input  DATA,
  input  CLOCK,
  output nQ,
  output Q
);

  wire nand_1_out, nand_3_out, nand_4_out, nand_5_out;

  nand nand_1 (nand_1_out, DATA, nand_3_out);
  nand nand_2 (nQ, nand_3_out, Q);
  nand nand_3 (nand_3_out, nand_1_out, CLOCK, nand_4_out);
  nand nand_4 (nand_4_out, CLOCK, nand_5_out);
  nand nand_5 (nand_5_out, nand_4_out, nand_1_out);
  nand nand_6 (Q, nQ, nand_4_out);
endmodule
