// Logisim project 1_to_4_demux.circ as structural Verilog: 1 circuit, main circuit main
module main (
  input  DATA,
  input  SELECT_A,
  input  SELECT_B,
  output [3:0] out_4
);

  wire not_1_out, not_2_out;

  not not_1 (not_1_out, SELECT_A);
  not not_2 (not_2_out, SELECT_B);
  and and_1 (out_4[0], not_1_out, not_2_out, DATA);
  and and_2 (out_4[1], not_1_out, SELECT_B, DATA);
  and and_3 (out_4[2], SELECT_A, not_2_out, DATA);
  and and_4 (out_4[3], SELECT_A, SELECT_B, DATA);
endmodule
