// Logisim project 4_to_1_mux.circ as structural Verilog: 1 circuit, main circuit main
module main (
  input  SELECT_A,
  input  SELECT_B,
  input  [3:0] INPUT,
  output out_4
);

  wire and_1_out, and_2_out, and_3_out, and_4_out, not_1_out, not_2_out;

  not not_1 (not_1_out, SELECT_A);
  not not_2 (not_2_out, SELECT_B);
  and and_1 (and_1_out, INPUT[0], not_2_out, not_1_out);
  and and_2 (and_2_out, INPUT[1], not_2_out, SELECT_A);
  and and_3 (and_3_out, INPUT[2], SELECT_B, not_1_out);
  and and_4 (and_4_out, INPUT[3], SELECT_B, SELECT_A);
  or or_1 (out_4, and_1_out, and_2_out, and_3_out, and_4_out);
endmodule
