// Logisim project 8bit_A_B_switch.circ as structural Verilog: 1 circuit, main circuit n
module n (
  input  [7:0] INPUT_A,
  input  [7:0] INPUT_B,
  input  A_B,
  output [7:0] out_4
);

  wire not_1_out, transistor_1_out, transistor_3_out, transistor_5_out, transistor_6_out, transistor_8_out,
       transistor_10_out, transistor_12_out, transistor_15_out, transistor_17_out, transistor_18_out,
       transistor_20_out, transistor_21_out, transistor_24_out, transistor_26_out, transistor_27_out,
       transistor_30_out;

  not not_1 (not_1_out, A_B);
  Transistor transistor_1 (.in(1'b0), .out(transistor_1_out), .gate(INPUT_A[7]));
  Transistor transistor_2 (.in(1'b0), .out(transistor_1_out), .gate(A_B));
  Transistor transistor_3 (.in(1'b0), .out(transistor_3_out), .gate(INPUT_B[7]));
  Transistor transistor_4 (.in(1'b0), .out(transistor_3_out), .gate(not_1_out));
  Transistor transistor_5 (.in(1'b0), .out(transistor_5_out), .gate(INPUT_A[6]));
  Transistor transistor_6 (.in(1'b0), .out(transistor_6_out), .gate(A_B));
  Transistor transistor_7 (.in(1'b0), .out(transistor_5_out), .gate(A_B));
  Transistor transistor_8 (.in(1'b0), .out(transistor_8_out), .gate(INPUT_B[6]));
  Transistor transistor_9 (.in(1'b0), .out(transistor_8_out), .gate(not_1_out));
  Transistor transistor_10 (.in(1'b0), .out(transistor_10_out), .gate(not_1_out));
  Transistor transistor_11 (.in(1'b0), .out(transistor_6_out), .gate(INPUT_A[5]));
  Transistor transistor_12 (.in(1'b0), .out(transistor_12_out), .gate(INPUT_A[4]));
  Transistor transistor_13 (.in(1'b0), .out(transistor_12_out), .gate(A_B));
  Transistor transistor_14 (.in(1'b0), .out(transistor_10_out), .gate(INPUT_B[5]));
  Transistor transistor_15 (.in(1'b0), .out(transistor_15_out), .gate(INPUT_B[4]));
  Transistor transistor_16 (.in(1'b0), .out(transistor_15_out), .gate(not_1_out));
  Transistor transistor_17 (.in(1'b0), .out(transistor_17_out), .gate(INPUT_A[3]));
  Transistor transistor_18 (.in(1'b0), .out(transistor_18_out), .gate(A_B));
  Transistor transistor_19 (.in(1'b0), .out(transistor_17_out), .gate(A_B));
  Transistor transistor_20 (.in(1'b0), .out(transistor_20_out), .gate(INPUT_B[3]));
  Transistor transistor_21 (.in(1'b0), .out(transistor_21_out), .gate(not_1_out));
  Transistor transistor_22 (.in(1'b0), .out(transistor_20_out), .gate(not_1_out));
  Transistor transistor_23 (.in(1'b0), .out(transistor_18_out), .gate(INPUT_A[2]));
  Transistor transistor_24 (.in(1'b0), .out(transistor_24_out), .gate(INPUT_A[1]));
  Transistor transistor_25 (.in(1'b0), .out(transistor_24_out), .gate(A_B));
  Transistor transistor_26 (.in(1'b0), .out(transistor_26_out), .gate(A_B));
  Transistor transistor_27 (.in(1'b0), .out(transistor_27_out), .gate(INPUT_B[1]));
  Transistor transistor_28 (.in(1'b0), .out(transistor_21_out), .gate(INPUT_B[2]));
  Transistor transistor_29 (.in(1'b0), .out(transistor_27_out), .gate(not_1_out));
  Transistor transistor_30 (.in(1'b0), .out(transistor_30_out), .gate(not_1_out));
  Pull_Resistor #(.pull(1)) pull_resistor_1 (.node(transistor_24_out));
  Pull_Resistor #(.pull(1)) pull_resistor_2 (.node(transistor_26_out));
  Pull_Resistor #(.pull(1)) pull_resistor_3 (.node(transistor_18_out));
  Pull_Resistor #(.pull(1)) pull_resistor_4 (.node(transistor_17_out));
  Transistor transistor_31 (.in(1'b0), .out(transistor_26_out), .gate(INPUT_A[0]));
  Pull_Resistor #(.pull(1)) pull_resistor_5 (.node(transistor_21_out));
  Pull_Resistor #(.pull(1)) pull_resistor_6 (.node(transistor_30_out));
  Pull_Resistor #(.pull(1)) pull_resistor_7 (.node(transistor_20_out));
  Pull_Resistor #(.pull(1)) pull_resistor_8 (.node(transistor_27_out));
  Transistor transistor_32 (.in(1'b0), .out(transistor_30_out), .gate(INPUT_B[0]));
  Pull_Resistor #(.pull(1)) pull_resistor_9 (.node(transistor_6_out));
  Pull_Resistor #(.pull(1)) pull_resistor_10 (.node(transistor_12_out));
  Pull_Resistor #(.pull(1)) pull_resistor_11 (.node(transistor_1_out));
  Pull_Resistor #(.pull(1)) pull_resistor_12 (.node(transistor_5_out));
  Pull_Resistor #(.pull(1)) pull_resistor_13 (.node(transistor_15_out));
  Pull_Resistor #(.pull(1)) pull_resistor_14 (.node(transistor_10_out));
  Pull_Resistor #(.pull(1)) pull_resistor_15 (.node(transistor_8_out));
  Pull_Resistor #(.pull(1)) pull_resistor_16 (.node(transistor_3_out));
  or or_1 (out_4[6], transistor_8_out, transistor_5_out);
  or or_2 (out_4[7], transistor_3_out, transistor_1_out);
  or or_3 (out_4[5], transistor_10_out, transistor_6_out);
  or or_4 (out_4[4], transistor_15_out, transistor_12_out);
  or or_5 (out_4[2], transistor_21_out, transistor_18_out);
  or or_6 (out_4[3], transistor_20_out, transistor_17_out);
  or or_7 (out_4[1], transistor_27_out, transistor_24_out);
  or or_8 (out_4[0], transistor_30_out, transistor_26_out);

  // Notes on the sheet:
  //   OUTPUT
endmodule
