// Logisim project 8bit_latch_reg.circ as structural Verilog: 1 circuit, main circuit main
module main (
  input  CLOCK,
  input  [7:0] IN,
  output [7:0] OUT
);

  wire and_1_out, and_2_out, and_3_out, and_4_out, and_5_out, and_6_out, and_7_out, and_8_out, and_9_out,
       and_10_out, and_11_out, and_12_out, and_13_out, and_14_out, and_15_out, and_16_out, nor_2_out,
       nor_4_out, nor_6_out, nor_8_out, nor_10_out, nor_13_out, nor_14_out, nor_16_out, not_1_out, not_2_out,
       not_3_out, not_4_out, not_5_out, not_6_out, not_7_out, not_8_out;

  not not_1 (not_1_out, IN[7]);
  and and_1 (and_1_out, not_1_out, CLOCK);
  nor nor_1 (OUT[7], and_1_out, nor_2_out);
  and and_2 (and_2_out, CLOCK, IN[7]);
  nor nor_2 (nor_2_out, OUT[7], and_2_out);
  not not_2 (not_2_out, IN[6]);
  and and_3 (and_3_out, not_2_out, CLOCK);
  and and_4 (and_4_out, CLOCK, IN[6]);
  nor nor_3 (OUT[6], and_3_out, nor_4_out);
  and and_5 (and_5_out, not_3_out, CLOCK);
  nor nor_4 (nor_4_out, OUT[6], and_4_out);
  nor nor_5 (OUT[5], and_5_out, nor_6_out);
  not not_3 (not_3_out, IN[5]);
  and and_6 (and_6_out, CLOCK, IN[5]);
  nor nor_6 (nor_6_out, OUT[5], and_6_out);
  not not_4 (not_4_out, IN[4]);
  and and_7 (and_7_out, not_4_out, CLOCK);
  nor nor_7 (OUT[4], and_7_out, nor_8_out);
  and and_8 (and_8_out, CLOCK, IN[4]);
  nor nor_8 (nor_8_out, OUT[4], and_8_out);
  not not_5 (not_5_out, IN[3]);
  and and_9 (and_9_out, not_5_out, CLOCK);
  nor nor_9 (OUT[3], and_9_out, nor_10_out);
  and and_10 (and_10_out, CLOCK, IN[3]);
  nor nor_10 (nor_10_out, OUT[3], and_10_out);
  not not_6 (not_6_out, IN[2]);
  and and_11 (and_11_out, not_6_out, CLOCK);
  and and_12 (and_12_out, CLOCK, IN[2]);
  nor nor_11 (OUT[2], and_11_out, nor_13_out);
  and and_13 (and_13_out, not_7_out, CLOCK);
  nor nor_12 (OUT[1], and_13_out, nor_14_out);
  nor nor_13 (nor_13_out, OUT[2], and_12_out);
  not not_7 (not_7_out, IN[1]);
  and and_14 (and_14_out, CLOCK, IN[1]);
  nor nor_14 (nor_14_out, OUT[1], and_14_out);
  not not_8 (not_8_out, IN[0]);
  and and_15 (and_15_out, not_8_out, CLOCK);
  nor nor_15 (OUT[0], and_15_out, nor_16_out);
  and and_16 (and_16_out, CLOCK, IN[0]);
  nor nor_16 (nor_16_out, OUT[0], and_16_out);

  // Notes on the sheet:
  //   Input
  //   8-bit latch register
  //   Output
endmodule
