// Logisim project ripple_counter.circ as structural Verilog: 1 circuit, main circuit main
module main (
  input  CLK,
  output [7:0] out_2
);

  wire d_ff_1_q, d_ff_1_qn, d_ff_2_q, d_ff_2_qn, d_ff_3_q, d_ff_3_qn, d_ff_4_q, d_ff_4_qn, d_ff_5_q,
       d_ff_5_qn, d_ff_6_q, d_ff_6_qn, d_ff_7_q, d_ff_7_qn, d_ff_8_q, d_ff_8_qn;

  D_Flip_Flop d_ff_1 (.clk(CLK), .D(d_ff_1_qn), .Q(d_ff_1_q), .Qn(d_ff_1_qn));  // open: preset, en, reset
  not not_1 (out_2[0], d_ff_1_q);
  D_Flip_Flop d_ff_2 (.clk(d_ff_1_q), .D(d_ff_2_qn), .Q(d_ff_2_q), .Qn(d_ff_2_qn));  // open: preset, en, reset
  not not_2 (out_2[1], d_ff_2_q);
  D_Flip_Flop d_ff_3 (.clk(d_ff_2_q), .D(d_ff_3_qn), .Q(d_ff_3_q), .Qn(d_ff_3_qn));  // open: preset, en, reset
  not not_3 (out_2[2], d_ff_3_q);
  D_Flip_Flop d_ff_4 (.clk(d_ff_3_q), .D(d_ff_4_qn), .Q(d_ff_4_q), .Qn(d_ff_4_qn));  // open: preset, en, reset
  not not_4 (out_2[3], d_ff_4_q);
  D_Flip_Flop d_ff_5 (.clk(d_ff_4_q), .D(d_ff_5_qn), .Q(d_ff_5_q), .Qn(d_ff_5_qn));  // open: preset, en, reset
  not not_5 (out_2[4], d_ff_5_q);
  D_Flip_Flop d_ff_6 (.clk(d_ff_5_q), .D(d_ff_6_qn), .Q(d_ff_6_q), .Qn(d_ff_6_qn));  // open: preset, en, reset
  not not_6 (out_2[5], d_ff_6_q);
  D_Flip_Flop d_ff_7 (.clk(d_ff_6_q), .D(d_ff_7_qn), .Q(d_ff_7_q), .Qn(d_ff_7_qn));  // open: preset, en, reset
  not not_7 (out_2[6], d_ff_7_q);
  D_Flip_Flop d_ff_8 (.clk(d_ff_7_q), .D(d_ff_8_qn), .Q(d_ff_8_q), .Qn(d_ff_8_qn));  // open: preset, en, reset
  not not_8 (out_2[7], d_ff_8_q);

  // Notes on the sheet:
  //   8-bit Ripple Counter using J/K Flip Flops
endmodule
